# Fritzing sketch matrix_fritzing (saved by Fritzing 0.9.3b)
breadboards: 2

parts:
  R2 = Resistor [tolerance=±5% resistance=330 package=THT]
  R4 = Resistor [tolerance=±5% resistance=330 package=THT]
  R5 = Resistor [tolerance=±5% resistance=330 package=THT]
  R6 = Resistor [tolerance=±5% resistance=330 package=THT]
  R7 = Resistor [tolerance=±5% resistance=330 package=THT]
  R8 = Resistor [tolerance=±5% resistance=330 package=THT]
  Disp1 = LBT2088AH [part_number=LBT2088AH]
  R10 = Resistor [tolerance=±5% resistance=330 package=THT]
  Part1 = Arduino Uno (Rev3)
  R11 = Resistor [tolerance=±5% resistance=330 package=THT]

nets:
  N1: R2.Pin_0, Disp1.pin_13
  N2: R2.Pin_1, Part1.D2
  N3: R4.Pin_0, Disp1.pin_4
  N4: R4.Pin_1, Part1.D4
  N5: R5.Pin_0, Disp1.pin_10
  N6: R5.Pin_1, Part1.D5_PWM
  N7: R6.Pin_0, Disp1.pin_6
  N8: R6.Pin_1, Part1.D6_PWM
  N9: R7.Pin_0, Disp1.pin_11
  N10: R7.Pin_1, Part1.D7
  N11: R8.Pin_0, Disp1.pin_15
  N12: R8.Pin_1, Part1.D8
  N13: Disp1.pin1, Part1.A0
  N14: Disp1.pin2, Part1.A2
  N15: Disp1.pin_3, R10.Pin_0
  N16: Disp1.pin_5, Part1.A3
  N17: Disp1.pin_7, Part1.A1
  N18: Disp1.pin_8, Part1.D12/MISO
  N19: Disp1.pin_9, Part1.D10_PWM/SS
  N20: Disp1.pin_12, Part1.D13/SCK
  N21: Disp1.pin_14, Part1.D11_PWM/MOSI
  N22: Disp1.pin_16, R11.Pin_0
  N23: R10.Pin_1, Part1.D3_PWM
  N24: Part1.D9_PWM, R11.Pin_1
